// Logisim project FPGANeuralNetwork.circ as structural Verilog
module HiddenLayer (
  input  RESET,
  input  [31:0] WEIGHTS1,
  input  [31:0] NN_INPUT,
  input  [31:0] WEIGHTS2,
  input  [31:0] WEIGHTS3,
  output [7:0] HIDDENLAYER_OUT
);

  wire adder_1_cout, switch_1_p1;
  wire [7:0] adder_1_out, adder_2_out, neuron_1_neuron_out, neuron_2_neuron_out, neuron_3_neuron_out;

  // Switch switch_1: pin names not known; wires that end beside it: switch_1_p1
  Neuron neuron_1 (
    .RESET(RESET), .INPUT1(NN_INPUT[7:0]), .INPUT2(NN_INPUT[15:8]), .INPUT3(NN_INPUT[23:16]),
    .INPUT4(NN_INPUT[31:24]), .WEIGHT1(NN_INPUT[7:0]), .WEIGHT2(NN_INPUT[15:8]), .WEIGHT3(NN_INPUT[23:16]),
    .WEIGHT4(NN_INPUT[31:24]), .ENABLE(switch_1_p1), .NEURON_OUT(neuron_1_neuron_out));
  Neuron neuron_2 (
    .RESET(RESET), .INPUT1(NN_INPUT[7:0]), .INPUT2(NN_INPUT[15:8]), .INPUT3(NN_INPUT[23:16]),
    .INPUT4(NN_INPUT[31:24]), .WEIGHT1(WEIGHTS2[7:0]), .WEIGHT2(WEIGHTS2[15:8]), .WEIGHT3(WEIGHTS2[23:16]),
    .WEIGHT4(WEIGHTS2[31:24]), .ENABLE(switch_1_p1), .NEURON_OUT(neuron_2_neuron_out));
  Neuron neuron_3 (
    .RESET(RESET), .INPUT1(NN_INPUT[7:0]), .INPUT2(NN_INPUT[15:8]), .INPUT3(NN_INPUT[23:16]),
    .INPUT4(NN_INPUT[31:24]), .WEIGHT1(WEIGHTS3[7:0]), .WEIGHT2(WEIGHTS3[15:8]), .WEIGHT3(WEIGHTS3[23:16]),
    .WEIGHT4(WEIGHTS3[31:24]), .ENABLE(switch_1_p1), .NEURON_OUT(neuron_3_neuron_out));
  Adder adder_1 (
    .a(neuron_1_neuron_out), .b(neuron_2_neuron_out), .out(adder_1_out), .cout(adder_1_cout));  // open: cin
  Adder adder_2 (.a(adder_1_out), .b(neuron_3_neuron_out), .out(adder_2_out), .cin(adder_1_cout));  // open: cout
  Divider divider_1 (.a(adder_2_out), .out(HIDDENLAYER_OUT));  // open: b, upper, rem

  assign WEIGHTS1 = NN_INPUT;
endmodule

module main (
  input  reset
);

  wire [7:0] hiddenlayer_1_hiddenlayer_out;
  wire [31:0] weight1_q, weight2_q, weight3_q;

  Register #(.width(32)) weight2 (.Q(weight2_q));  // open: D, en, clk, clr
  Register #(.width(32)) weight3 (.Q(weight3_q));  // open: D, en, clk, clr
  Register #(.width(32)) weight1 (.Q(weight1_q));  // open: D, en, clk, clr
  HiddenLayer hiddenlayer_1 (
    .RESET(reset), .WEIGHTS1(weight1_q), .WEIGHTS2(weight2_q), .WEIGHTS3(weight3_q),
    .HIDDENLAYER_OUT(hiddenlayer_1_hiddenlayer_out));  // open: NN_INPUT
  Sigmoid_Activation_Function sigmoid_activation_function_1 (.x(hiddenlayer_1_hiddenlayer_out));  // open: y
endmodule

module Neuron (
  input  RESET,
  input  [7:0] INPUT1,
  input  [7:0] INPUT2,
  input  [7:0] INPUT3,
  input  [7:0] INPUT4,
  input  [7:0] WEIGHT1,
  input  [7:0] WEIGHT2,
  input  [7:0] WEIGHT3,
  input  [7:0] WEIGHT4,
  input  ENABLE,
  output [7:0] NEURON_OUT
);

  wire [1:0] counter_1_q;
  wire [7:0] multiplexer_1_out, multiplexer_2_out, multiplier_1_out;

  Counter #(.max('h3), .width(2)) counter_1 (
    .clr(ENABLE), .up(ENABLE), .Q(counter_1_q));  // open: load, count, clk, D, carry
  Multiplexer #(.select(2), .width(8)) multiplexer_1 (
    .in0(INPUT1), .in1(INPUT2), .in2(INPUT3), .in3(INPUT4), .out(multiplexer_1_out), .sel(counter_1_q));
  Multiplexer #(.select(2), .width(8)) multiplexer_2 (
    .in0(WEIGHT1), .in1(WEIGHT2), .in2(WEIGHT3), .in3(WEIGHT4), .out(multiplexer_2_out), .sel(counter_1_q));
  Register register_1 (.D(multiplier_1_out), .en(ENABLE), .clk(ENABLE), .Q(NEURON_OUT));  // open: clr
  Multiplier multiplier_1 (.a(multiplexer_1_out), .b(multiplexer_2_out), .out(multiplier_1_out));  // open: cin, cout

  assign RESET = ENABLE;
endmodule

// VHDL entity Sigmoid_Activation_Function, as the project stores it:
--------------------------------------------------------------------------------
-- Project : Hardware_Implemented_Neural_Network
-- File    : 
-- Autor   :
-- Date    : 
--
--------------------------------------------------------------------------------
-- Description : 
-- This is a sigmoid function that takes an 8-bit input vector and outputs an 8-bit result vector.
--
--------------------------------------------------------------------------------

LIBRARY ieee;
USE ieee.std_logic_1164.all;

ENTITY Sigmoid_Activation_Function IS
  PORT (
  ------------------------------------------------------------------------------
  --Insert input ports below
    x        	: IN  std_logic_vector(7 DOWNTO 0); -- input vector example
  ------------------------------------------------------------------------------
  --Insert output ports below
    y        	: OUT std_logic_vector(7 DOWNTO 0)  -- output vector example
    );
END Sigmoid_Activation_Function;

--------------------------------------------------------------------------------
-- VHDL Description
--------------------------------------------------------------------------------

-- Sigmoid function output formula: y = 1 / (1 + e^-x)

ARCHITECTURE Behavioural OF Sigmoid_Activation_Function IS

-- creates a 16-bit wide intermediate signal to aid calculatons
signal temp : std_logic_vector(15 downto 0);

BEGIN

-- takes the negation of our input, and pads it with zeroes to make it 16 bits wide to be saved to the intermediate signal "temp"
temp <= NOT x + "0000000000000001";

-- takes the square negation of our input to save to output "y".
y <= std_logic_vector(unsigned(temp)*unsigned(temp));

END Behavioral;

// VHDL entity weight_register, as the project stores it:
--------------------------------------------------------------------------------
-- Project : Hardware_Implemented_Neural_Network
-- File    : 
-- Autor   :
-- Date    :
--
--------------------------------------------------------------------------------
-- Description : 
-- This is a weight register that takes in data and outputs it on the next clock cycle.
--
--------------------------------------------------------------------------------

-- The weight_register entity has a clock (clk), reset (rst), data, and queue port. 
-- When the reset port is high, the temp signal is set to all 0's. When the clock 
-- port is high (on the rising edge), the temp signal is set to the data. The queue 
-- port is always equal to the temp signal.


LIBRARY IEEE;
USE IEEE.std_logic_1164.ALL;

entity weight_register is
    port(
        clk : IN std_logic;
        rst : IN std_logic;
        data : IN std_logic_vector(7 DOWNTO 0);
        queue : OUT std_logic_vector(7 DOWNTO 0)
    );
END weight_register;

ARCHITECTURE Behavioral OF weight_register IS

signal temp : std_logic_vector(7 DOWNTO 0);
    
BEGIN

process(clk, rst)
BEGIN
   IF(rst='1') THEN
       temp <= (OTHERS => '0');
   ELSIF(rising_edge(clk)) THEN
       temp <= data;
   END IF;
END PROCESS;

queue <= temp;
    
END Behavioral;

// VHDL entity gradient_descent, as the project stores it:
--------------------------------------------------------------------------------
-- Project : Hardware_Implemented_Neural_Network
-- File    :
-- Autor   :
-- Date    : 
--
--------------------------------------------------------------------------------
-- Description : 
-- This is a gradient descent algorithm implemented in VHDL.
-- The purpose of the algorithm is to find the weights that minimize the error between the predicted values and the actual values. 
-- The inputs to the entity are the data (x) and the actual values (y). The clock (clk) and reset (rst) signals are also inputs.
-- The output (done) is '1' when the predicted values match the actual values. 
-- The algorithm consists of four states. In state 0, the error is calculated for each bit of data.
-- In state 1, the delta is calculated. In state 2, the weights are updated. In state 3, the predicted values are updated.
--
--------------------------------------------------------------------------------

LIBRARY IEEE;
USE IEEE.STD_LOGIC_1164.all;

ENTITY gradient_descent IS
PORT(
    x : IN std_logic_vector(7 downto 0);
    y : IN std_logic_vector(7 downto 0);
    clk : IN std_logic;
    rst : IN std_logic;
    done : OUT std_logic
    );
END gradient_descent;

--------------------------------------------------------------------------------
--Complete your VHDL description below
--------------------------------------------------------------------------------

ARCHITECTURE Behavioral OF gradient_descent IS

signal state : integer range 0 to 3 := 0;
signal count : integer range 0 to 7 := 0;
signal error : std_logic_vector(3 downto 0) := (others => '0');
signal y_hat : std_logic_vector(7 downto 0) := (others => '0');
signal delta : std_logic_vector(3 downto 0) := (others => '0');
signal weight : std_logic_vector(3 downto 0) := "0001";
constant learning_rate : real := 0.1;

BEGIN

process(clk, rst)
begin
    if(rst = '1') then
        state <= 0;
        count <= 0;
        error <= (others => '0');
        y_hat <= (others => '0');
    elsif(rising_edge(clk)) then
        case state is
            when 0 =>
                if(count < 8) then
                    error <= error + (x(count) xor y_hat(count));
                    count <= count + 1;
                else
                    count <= 0;
                    state <= 1;
                end if;
            when 1 =>
                delta <= error * weight;
                state <= 2;
            when 2 =>
                weight <= weight - (learning_rate * delta);
                state <= 3;
            when 3 =>
                state <= 0;
                y_hat <= y_hat + delta;
        end case;
    end if;
end process;

done <= '1' when y_hat = y else '0';

END Behavioral;
